# Fritzing sketch touch-lamp (saved by Fritzing 0.9.3b)
perfboards: 1

parts:
  CONN1 = USB connector [package=THT]  # not connected
  U2 = CAPSENSE_PAD [package=capsense_pad]
  R1 = Resistor [tolerance=±5% resistance=1M package="0402 [SMD]"]
  U3 = RELAY [package=relay-g5q]  # not connected
  Part1 = Arduino Pro Mini (5V)  # not connected

nets:
  N1: U2.RES, R1.Pin_1
